# Fritzing sketch HologramHand (saved by Fritzing 0.9.3b)
breadboards: 2

parts:
  R1 = Basic Flex Resistor
  R2 = Basic Flex Resistor
  R3 = Basic Flex Resistor
  Componente2 = Bluetooth HC-05 Macho
  LED2 = LEDs [package=led10mm]
  VCC1 = 4 x AAA Battery Mount
  R4 = Resistor [tolerance=±5% resistance=35 package="2512 [SMD]"]
  LED3 = RGB LED (com. anode, rbg) [package="5 mm [THT]"]
  R5 = Resistor [tolerance=±5% resistance=330 package="2512 [SMD]"]
  R7 = Resistor [tolerance=±5% resistance=330 package="2512 [SMD]"]
  R8 = Resistor [tolerance=±5% resistance=330 package="2512 [SMD]"]
  GY1 = MPU-6050 Board GY-521 [form="♀ (female)" package=THT]
  R9 = Resistor [tolerance=±5% resistance=10k package="2512 [SMD]"]
  R10 = Resistor [tolerance=±5% resistance=10k package="2512 [SMD]"]
  R11 = Resistor [tolerance=±5% resistance=10k package="2512 [SMD]"]
  Componente3 = Arduino Uno (Rev3)
  Componente4 = Arduino Uno (Rev3)  # not connected
  R12 = Basic Flex Resistor
  R13 = Basic Flex Resistor
  R14 = Basic Flex Resistor
  Componente5 = Bluetooth HC-05 Macho
  R15 = Resistor [tolerance=±5% resistance=35 package="2512 [SMD]"]
  GY2 = MPU-6050 Board GY-521 [form="♀ (female)" package=THT]
  VCC2 = 4 x AAA Battery Mount
  LED6 = LEDs [package=led10mm]
  LED8 = RGB LED (com. anode, rbg) [package="5 mm [THT]"]
  R22 = Resistor [tolerance=±5% resistance=330 package="2512 [SMD]"]
  R23 = Resistor [tolerance=±5% resistance=330 package="2512 [SMD]"]
  R24 = Resistor [tolerance=±5% resistance=330 package="2512 [SMD]"]
  R25 = Resistor [tolerance=±5% resistance=10k package="2512 [SMD]"]
  R26 = Resistor [tolerance=±5% resistance=10k package="2512 [SMD]"]
  R27 = Resistor [tolerance=±5% resistance=10k package="2512 [SMD]"]
  Componente6 = Adafruit Proto Shield R3 [part_number="Adafruit #2077"]

nets:
  N1: R1.Pin_2, R10.Pin_1, Componente3.A1
  GND: R1.pin_1, R2.pin_1, R3.pin_1, Componente2.GND, LED2.C, VCC1.-, LED3.common_anode, GY1.pin2, Componente3.GND
  N2: R2.Pin_2, R9.Pin_1, Componente3.A0
  N3: R3.Pin_2, R11.Pin_1, Componente3.A2
  N4: Componente2.TXD, Componente3.D7
  N5: Componente2.RXD, Componente3.D8
  VCC: Componente2.VCC, VCC1.+, GY1.pin1, R9.Pin_0, R10.Pin_0, R11.Pin_0, Componente3.5V
  N6: LED2.A, R4.Pin_1
  N7: R4.Pin_0, Componente3.D5_PWM
  N8: LED3.red_cathode, R8.Pin_1
  N9: LED3.blue_cathode, R5.Pin_1
  N10: LED3.green_cathode, R7.Pin_1
  N11: R5.Pin_0, Componente3.D3_PWM
  N12: R7.Pin_0, Componente3.D2
  N13: R8.Pin_0, Componente3.D4
  N14: GY1.pin3, Componente3.A5/SCL
  N15: GY1.pin4, Componente3.A4/SDA
  N16: R12.Pin_2, R25.Pin_1, Componente6.A3
  N17: R12.pin_1, R13.pin_1, R14.pin_1, Componente5.GND, GY2.pin2, VCC2.-, LED6.C, LED8.common_anode
  N18: R13.Pin_2, R27.Pin_1, Componente6.A1
  N19: R14.Pin_2, R26.Pin_1, Componente6.A2
  N20: Componente5.TXD, Componente6.D0
  N21: Componente5.RXD, Componente6.D1
  N22: Componente5.VCC, GY2.pin1, VCC2.+, R25.Pin_0, R26.Pin_0, R27.Pin_0
  N23: R15.Pin_0, Componente6.D5
  N24: R15.Pin_1, LED6.A
  N25: GY2.pin3, Componente6.A5
  N26: GY2.pin4, Componente6.A4
  N27: LED8.red_cathode, R22.Pin_1
  N28: LED8.blue_cathode, R23.Pin_1
  N29: LED8.green_cathode, R24.Pin_1
  N30: R22.Pin_0, Componente6.D4
  N31: R23.Pin_0, Componente6.D3
  N32: R24.Pin_0, Componente6.D2

notes:
  Valores Resistencias
  LED RGB: 330Ω
  LED AZUL: 35Ω
  FLEX: 10kΩ

custom parts:
  MPU-6050 Board GY-521: Acelerometro y Giroscopio MPU-6050 Board GY-521
  Adafruit Proto Shield R3: This prototyping shield is the best out there (well, we think so, at least), and now is even better with Version R3 - updated for the most compatibility with just about all the Arduinos! It works with UNO, Mega, Leonardo, NG, Diecimila, Duemilanove, and compatible Arduinos. Yun's and Arduino Ethernets have a chunky Ethernet jack that gets in the way of stacking, you can use the stacking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
